// Logisim project edbs.circ as structural Verilog: 1 circuit, main circuit main
module main (
  input  [7:0] Minuend,
  input  [7:0] Difference,
  input  [7:0] Subtrahend
);

  wire subtractor_1_bout, subtractor_2_bout, subtractor_3_bout, subtractor_4_bout, subtractor_5_bout,
       subtractor_6_bout, subtractor_7_bout;
  wire [7:0] subtractor_1_out;

  // Probe on Subtrahend
  // Probe on Minuend
  Subtractor #(.width(1)) subtractor_1 (
    .a(Minuend[0]), .b(Subtrahend[0]), .out(subtractor_1_out[0]), .bout(subtractor_1_bout));  // open: bin
  Subtractor #(.width(1)) subtractor_2 (
    .a(Minuend[1]), .b(Subtrahend[1]), .out(subtractor_1_out[1]), .bin(subtractor_1_bout),
    .bout(subtractor_2_bout));
  Subtractor #(.width(1)) subtractor_3 (
    .a(Minuend[2]), .b(Subtrahend[2]), .out(subtractor_1_out[2]), .bin(subtractor_2_bout),
    .bout(subtractor_3_bout));
  Subtractor #(.width(1)) subtractor_4 (
    .a(Minuend[3]), .b(Subtrahend[3]), .out(subtractor_1_out[3]), .bin(subtractor_3_bout),
    .bout(subtractor_4_bout));
  Subtractor #(.width(1)) subtractor_5 (
    .a(Minuend[4]), .b(Subtrahend[4]), .out(subtractor_1_out[4]), .bin(subtractor_4_bout),
    .bout(subtractor_5_bout));
  Subtractor #(.width(1)) subtractor_6 (
    .a(Minuend[5]), .b(Subtrahend[5]), .out(subtractor_1_out[5]), .bin(subtractor_5_bout),
    .bout(subtractor_6_bout));
  Subtractor #(.width(1)) subtractor_7 (
    .a(Minuend[6]), .b(Subtrahend[6]), .out(subtractor_1_out[6]), .bin(subtractor_6_bout),
    .bout(subtractor_7_bout));
  Subtractor #(.width(1)) subtractor_8 (
    .a(Minuend[7]), .b(Subtrahend[7]), .out(subtractor_1_out[7]), .bin(subtractor_7_bout));  // open: bout
  // Probe on subtractor_1_out
endmodule
